// Logisim project ex1.circ as structural Verilog: 1 circuit, main circuit Split
module Split (
  input  [7:0] IN1,
  output OUT1,
  output OUT2,
  output [8:0] OUT3,
  output [8:0] OUT4
);

  wire xor_1_out, xor_2_out, xor_3_out, xor_4_out, xor_5_out, xor_6_out;
  wire [3:0] bitadder_1_out, bitadder_2_out;
  wire [7:0] i0_out, not_2_out;
  wire [8:0] bit_extender_1_out, bit_extender_2_out;

  not not_1 (OUT3[8], OUT1);
  xor xor_1 (xor_1_out, IN1[0], IN1[1]);
  xor xor_2 (xor_2_out, IN1[2], IN1[3]);
  xor xor_3 (xor_3_out, IN1[4], IN1[5]);
  xor xor_4 (xor_4_out, IN1[6], IN1[7]);
  xor xor_5 (xor_5_out, xor_1_out, xor_2_out);
  xor xor_6 (xor_6_out, xor_3_out, xor_4_out);
  xor xor_7 (OUT1, xor_5_out, xor_6_out);
  xor i0 (i0_out[0], OUT2, IN1[0]);
  xor xor_8 (i0_out[7], OUT2, IN1[7]);
  assign not_2_out = ~IN1;  // NOT_Gate not_2, 8 bits wide
  xor xor_9 (i0_out[1], OUT2, IN1[1]);
  xor xor_10 (i0_out[6], OUT2, IN1[6]);
  BitAdder bitadder_1 (.in0(IN1), .out(bitadder_1_out));
  BitAdder bitadder_2 (.in0(not_2_out), .out(bitadder_2_out));
  xor xor_11 (i0_out[2], OUT2, IN1[2]);
  xor xor_12 (i0_out[5], OUT2, IN1[5]);
  xor i4 (i0_out[4], OUT2, IN1[4]);
  Comparator #(.width(4), .mode("unsigned")) comparator_1 (
    .a(bitadder_1_out), .b(bitadder_2_out), .gt(OUT2));  // open: eq, lt
  xor xor_13 (i0_out[3], OUT2, IN1[3]);
  assign bit_extender_1_out = {{8{1'b0}}, OUT2};  // Bit_Extender bit_extender_1
  Bit_Extender #(.in_width(9), .out_width(9)) bit_extender_2 (.in({OUT2, i0_out}), .out(bit_extender_2_out));
  Adder #(.width(9)) adder_1 (.a(bit_extender_1_out), .b(bit_extender_2_out), .out(OUT4));  // open: cin, cout

  assign OUT3[7:0] = IN1;

  // Other names for the same wires on the sheet: IN1_0 = IN1[0]; IN1_1 = IN1[1]; IN1_2 = IN1[2]; IN1_3 = IN1[3];
  //   IN1_4 = IN1[4]; IN1_5 = IN1[5]; IN1_6 = IN1[6]; IN1_7 = IN1[7]

  // Notes on the sheet:
  //   PUT CIRCUITRY HERE
endmodule
