// Logisim project ex3.circ as structural Verilog: 2 circuits, main circuit rot1
module rot1 (
  input  [7:0] in_1,
  output [7:0] out_2
);


  assign out_2 = {in_1[0], in_1[7:1]};

  // Notes on the sheet:
  //   PUT CIRCUITRY HERE
endmodule

module Running_LED (
  input  [7:0] INITIAL_LED,
  input  RST,
  output [7:0] OUT_LED,
  output out_4
);

  wire clock_1_out, clock_2_out, clock_3_out, register_2_q;
  wire [7:0] multiplexer_1_out, register_1_q;

  Clock clock_1 (.out(clock_1_out));
  LED led_1 (.in(OUT_LED[7]));
  LED led_2 (.in(OUT_LED[6]));
  Multiplexer #(.width(8), .enable("false")) multiplexer_1 (
    .in0(OUT_LED), .in1(INITIAL_LED), .out(multiplexer_1_out), .sel(RST));
  LED led_3 (.in(OUT_LED[5]));
  Register register_1 (.D(multiplexer_1_out), .clk(clock_1_out), .Q(register_1_q));  // open: en, clr
  Clock #(.lowDuration(7)) clock_2 (.out(clock_2_out));
  Clock clock_3 (.out(clock_3_out));
  LED led_4 (.in(OUT_LED[4]));
  rot1 rot1_1 (.in_1(register_1_q), .out_2(OUT_LED));
  Register #(.width(1)) register_2 (.D(clock_2_out), .clk(clock_3_out), .Q(register_2_q));  // open: en, clr
  LED led_5 (.in(OUT_LED[3]));
  Register #(.width(1)) register_3 (.D(register_2_q), .clk(clock_3_out), .Q(out_4));  // open: en, clr
  LED led_6 (.in(OUT_LED[2]));
  LED led_7 (.in(OUT_LED[1]));
  LED led_8 (.in(OUT_LED[0]));
  ROM rom_1 ();  // open: addr, data

  // Notes on the sheet:
  //   PUT CIRCUITS HERE
endmodule
