// Logisim project ex2_test.circ as structural Verilog: 1 circuit, main circuit main
module main (
  output [7:0] out_1,
  output [15:0] Out1,
  output [15:0] out_3,
  output [3:0] out_4
);

  wire clock_1_out;
  wire [7:0] adder_1_out;

  Clock clock_1 (.out(clock_1_out));
  Adder adder_1 (.a(8'h1), .b(out_1), .out(adder_1_out));  // open: cin, cout
  Register register_1 (.D(adder_1_out), .clk(clock_1_out), .Q(out_1));  // open: en, clr
  ROM #(.dataWidth(16)) rom_1 (.addr(out_1), .data(out_3));
  ROM #(.dataWidth(4)) rom_2 (.addr(out_1), .data(out_4));
  rotr rotr_1 (.A(out_3), .B(out_4), .Out1(Out1));

  // Other names for the same wires on the sheet: A[15:0] = out_3; B[3:0] = out_4; Test[7:0] = out_1

  // Notes on the sheet:
  //   contents of rom_1 (hex, n*v repeats v):
  //   16*1
  //   Your rotr circuit must fit here!
  //   contents of rom_2 (hex, n*v repeats v):
  //   0 1 2 3 4 5 6 7 8 9 a b c d e f
  //   There should be no red or blue wires, and the result should not be all X's
endmodule
