// Logisim project ex3_test.circ as structural Verilog: 1 circuit, main circuit main
module main (
  output [7:0] out_1,
  output [7:0] Out_LED,
  output [7:0] out_3,
  output out_4
);

  wire clock_1_out;
  wire [7:0] adder_1_out;

  Clock clock_1 (.out(clock_1_out));
  Adder adder_1 (.a(8'h1), .b(out_1), .out(adder_1_out));  // open: cin, cout
  Register register_1 (.D(adder_1_out), .clk(clock_1_out), .Q(out_1));  // open: en, clr
  ROM rom_1 (.addr(out_1), .data(out_3));
  Running_LED running_led_1 (.INITIAL_LED(out_3), .RST(out_4), .OUT_LED(Out_LED));  // open: out_4
  ROM #(.dataWidth(1)) rom_2 (.addr(out_1));  // open: data

  // Other names for the same wires on the sheet: INITIAL_LED[7:0] = out_3; RST = out_4; Test[7:0] = out_1

  // Notes on the sheet:
  //   contents of rom_1 (hex, n*v repeats v):
  //   1 80 81 ff f0 f
  //   Your Split circuit must fit here!
  //   There should be no red or blue wires, and the result should not be all X's
  //   contents of rom_2 (hex, n*v repeats v):
  //   1
endmodule
