// Logisim project ex1.circ as structural Verilog: 6 circuits, main circuit main
module main (
  output [7:0] non_pipe_out,
  output [7:0] t1out,
  output [7:0] pi
);

  wire CLK_out;
  wire [7:0] Address_Counter_q, rom_1_data;

  Counter Address_Counter (.clk(CLK_out), .Q(Address_Counter_q));  // open: clr, load, up, count, D, carry
  Clock CLK (.out(CLK_out));
  ROM rom_1 (.addr(Address_Counter_q), .data(rom_1_data));
  // Probe on non_pipe_out
  non_pipelined non_pipelined_1 (.in1(rom_1_data[3:0]), .in2(rom_1_data[7:4]), .CLK(CLK_out), .out1(non_pipe_out));
  // Probe on t1out
  t1 t1_1 (.in1(rom_1_data[3:0]), .in2(rom_1_data[7:4]), .CLK(CLK_out), .OUT1(t1out));
  pipelined pipelined_1 (.in1(rom_1_data[3:0]), .in2(rom_1_data[7:4]), .CLK(CLK_out), .out1(pi));
  // Probe on pi

  // Notes on the sheet:
  //   contents of rom_1 (hex, n*v repeats v):
  //   13 a2 fc 8f 1c 2 b0
endmodule

module non_pipelined (
  input  [3:0] in1,
  input  [3:0] in2,
  input  CLK,
  output [7:0] out1
);

  wire [7:0] move_and_add_1_moved_multiplicand, move_and_add_1_result, move_and_add_2_moved_multiplicand,
       move_and_add_2_result, move_and_add_3_moved_multiplicand, move_and_add_3_result, move_and_add_4_result;

  // Probe on move_and_add_1_result
  move_and_add move_and_add_1 (
    .multiplicand({4'b0000, in1}), .result(move_and_add_1_result), .current({8{1'b0}}), .multiplier(in2[0]),
    .moved_multiplicand(move_and_add_1_moved_multiplicand));
  move_and_add move_and_add_2 (
    .multiplicand(move_and_add_1_moved_multiplicand), .result(move_and_add_2_result),
    .current(move_and_add_1_result), .multiplier(in2[1]),
    .moved_multiplicand(move_and_add_2_moved_multiplicand));
  move_and_add move_and_add_3 (
    .multiplicand(move_and_add_2_moved_multiplicand), .result(move_and_add_3_result),
    .current(move_and_add_2_result), .multiplier(in2[2]),
    .moved_multiplicand(move_and_add_3_moved_multiplicand));
  move_and_add move_and_add_4 (
    .multiplicand(move_and_add_3_moved_multiplicand), .result(move_and_add_4_result),
    .current(move_and_add_3_result), .multiplier(in2[3]));  // open: moved_multiplicand
  Register register_1 (.D(move_and_add_4_result), .clk(CLK), .Q(out1));  // open: en, clr
endmodule

module pipelined (
  input  [3:0] in1,
  input  [3:0] in2,
  input  CLK,
  output [7:0] out1
);

  wire register_3_q, register_4_q, register_5_q, register_8_q, register_9_q, register_12_q;
  wire [7:0] move_and_add_1_moved_multiplicand, move_and_add_1_result, move_and_add_2_moved_multiplicand,
       move_and_add_2_result, move_and_add_3_moved_multiplicand, move_and_add_3_result,
       move_and_add_4_result, register_1_q, register_2_q, register_6_q, register_7_q, register_10_q,
       register_11_q;

  move_and_add move_and_add_1 (
    .multiplicand({4'b0000, in1}), .result(move_and_add_1_result), .current({8{1'b0}}), .multiplier(in2[0]),
    .moved_multiplicand(move_and_add_1_moved_multiplicand));
  Register register_1 (.D(move_and_add_1_result), .clk(CLK), .Q(register_1_q));  // open: en, clr
  Register register_2 (.D(move_and_add_1_moved_multiplicand), .clk(CLK), .Q(register_2_q));  // open: en, clr
  Register #(.width(1)) register_3 (.D(in2[1]), .clk(CLK), .Q(register_3_q));  // open: en, clr
  Register #(.width(1)) register_4 (.D(in2[2]), .clk(CLK), .Q(register_4_q));  // open: en, clr
  Register #(.width(1)) register_5 (.D(in2[3]), .clk(CLK), .Q(register_5_q));  // open: en, clr
  move_and_add move_and_add_2 (
    .multiplicand(register_2_q), .result(move_and_add_2_result), .current(register_1_q),
    .multiplier(register_3_q), .moved_multiplicand(move_and_add_2_moved_multiplicand));
  Register register_6 (.D(move_and_add_2_result), .clk(CLK), .Q(register_6_q));  // open: en, clr
  Register register_7 (.D(move_and_add_2_moved_multiplicand), .clk(CLK), .Q(register_7_q));  // open: en, clr
  Register #(.width(1)) register_8 (.D(register_4_q), .clk(CLK), .Q(register_8_q));  // open: en, clr
  Register #(.width(1)) register_9 (.D(register_5_q), .clk(CLK), .Q(register_9_q));  // open: en, clr
  move_and_add move_and_add_3 (
    .multiplicand(register_7_q), .result(move_and_add_3_result), .current(register_6_q),
    .multiplier(register_8_q), .moved_multiplicand(move_and_add_3_moved_multiplicand));
  Register register_10 (.D(move_and_add_3_result), .clk(CLK), .Q(register_10_q));  // open: en, clr
  Register register_11 (.D(move_and_add_3_moved_multiplicand), .clk(CLK), .Q(register_11_q));  // open: en, clr
  Register #(.width(1)) register_12 (.D(register_9_q), .clk(CLK), .Q(register_12_q));  // open: en, clr
  move_and_add move_and_add_4 (
    .multiplicand(register_11_q), .result(move_and_add_4_result), .current(register_10_q),
    .multiplier(register_12_q));  // open: moved_multiplicand
  Register register_13 (.D(move_and_add_4_result), .clk(CLK), .Q(out1));  // open: en, clr

  // Other names for the same wires on the sheet: Clock = CLK
endmodule

module move_and_add (
  input  [7:0] current,
  input  [7:0] multiplicand,
  input  multiplier,
  output [7:0] result,
  output [7:0] moved_multiplicand
);

  wire [7:0] multiplexer_1_out;

  Multiplexer #(.width(8), .enable("false")) multiplexer_1 (
    .in0({8{1'b0}}), .in1(multiplicand), .out(multiplexer_1_out), .sel(multiplier));
  Adder adder_1 (.a(current), .b(multiplexer_1_out), .out(result));  // open: cin, cout
  Shifter shifter_1 (.in(multiplicand), .\dist (3'b001), .out(moved_multiplicand));
endmodule

module t1 (
  input  [3:0] in1,
  input  [3:0] in2,
  input  CLK,
  output [7:0] OUT1
);

  wire [7:0] adder_1_out, adder_2_out, adder_3_out, move_do_not_add_1_result, move_do_not_add_2_result,
       move_do_not_add_3_result, move_do_not_add_4_result, register_1_q, register_2_q, register_3_q,
       register_4_q;

  move_do_not_add move_do_not_add_1 (
    .multiplicand({4'b0000, in2}), .multiplier(in1[0]), .result(move_do_not_add_1_result));
  move_do_not_add move_do_not_add_2 (
    .multiplicand({3'b000, in2, 1'b0}), .multiplier(in1[1]), .result(move_do_not_add_2_result));
  move_do_not_add move_do_not_add_3 (
    .multiplicand({2'b00, in2, 2'b00}), .multiplier(in1[2]), .result(move_do_not_add_3_result));
  move_do_not_add move_do_not_add_4 (
    .multiplicand({1'b0, in2, 3'b000}), .multiplier(in1[3]), .result(move_do_not_add_4_result));
  Register register_1 (.D(move_do_not_add_1_result), .clk(CLK), .Q(register_1_q));  // open: en, clr
  Register register_2 (.D(move_do_not_add_2_result), .clk(CLK), .Q(register_2_q));  // open: en, clr
  Register register_3 (.D(move_do_not_add_3_result), .clk(CLK), .Q(register_3_q));  // open: en, clr
  Register register_4 (.D(move_do_not_add_4_result), .clk(CLK), .Q(register_4_q));  // open: en, clr
  Adder adder_1 (.a(register_1_q), .b(register_2_q), .out(adder_1_out));  // open: cin, cout
  Adder adder_2 (.a(register_3_q), .b(register_4_q), .out(adder_2_out));  // open: cin, cout
  Register register_5 (.D(adder_3_out), .clk(CLK), .Q(OUT1));  // open: en, clr
  Adder adder_3 (.a(adder_1_out), .b(adder_2_out), .out(adder_3_out));  // open: cin, cout

  // Other names for the same wires on the sheet: CLK1 = CLK
endmodule

module move_do_not_add (
  input  [7:0] multiplicand,
  input  multiplier,
  output [7:0] result
);

  Multiplexer #(.width(8), .enable("false")) multiplexer_1 (
    .in0({8{1'b0}}), .in1(multiplicand), .out(result), .sel(multiplier));
endmodule
