// Logisim project alu.circ as structural Verilog: 4 circuits, main circuit alu
module alu (
  input  [31:0] A,
  input  [31:0] B,
  input  [3:0] ALUSel,
  input  [2:0] in_4,
  input  [2:0] in_5,
  output [31:0] Result,
  output [2:0] out_7
);

  wire [0:0] Output13;
  wire [4:0] bit_extender_1_out, bit_extender_2_out, bit_extender_3_out;
  wire [6:0] Output15;
  wire [31:0] Output0, Output1, Output2, Output3, Output4, Output5, Output6, Output7, Output8, Output9,
       Output10, Output11, Output12, Output14;

  Subtractor #(.width(3)) subtractor_1 (.a(in_4), .b(in_5), .out(out_7));  // open: bin, bout
  Bit_Extender #(.in_width(32), .out_width(5)) bit_extender_1 (.in(B), .out(bit_extender_1_out));
  Bit_Extender #(.in_width(32), .out_width(5)) bit_extender_2 (.in(B), .out(bit_extender_2_out));
  Bit_Extender #(.in_width(32), .out_width(5)) bit_extender_3 (.in(B), .out(bit_extender_3_out));
  assign Output0 = A & B;  // AND_Gate and_1, 32 bits wide
  assign Output1 = A | B;  // OR_Gate or_1, 32 bits wide
  assign Output2 = A ^ B;  // XOR_Gate xor_1, 32 bits wide
  Adder #(.width(32)) adder_1 (.a(A), .b(B), .out(Output3));  // open: cin, cout
  Subtractor #(.width(32)) subtractor_2 (.a(A), .b(B), .out(Output4));  // open: bin, bout
  signed_mul1 signed_mul1_1 (.in1(A), .in2(B), .o1(Output5), .o2(Output7));
  Multiplier #(.width(32)) multiplier_1 (.a(A), .b(B), .cout(Output6));  // open: out, cin
  Divider #(.width(32)) divider_1 (.a(A), .b(B), .out(Output8), .rem(Output10));  // open: upper
  signed_divide signed_divide_1 (.in_1(A), .in_2(B), .out_3(Output9));
  Shifter #(.width(32), .shift("lr")) shifter_1 (.in(A), .\dist (bit_extender_1_out), .out(Output11));
  Shifter #(.width(32), .shift("ar")) shifter_2 (.in(A), .\dist (bit_extender_2_out), .out(Output12));
  Comparator #(.width(32)) comparator_1 (.a(A), .b(B), .lt(Output13[0]));  // open: gt, eq
  Shifter #(.width(32)) shifter_3 (.in(A), .\dist (bit_extender_3_out), .out(Output14));
  BitAdder #(.width(32)) bitadder_1 (.in0(A), .in1(B), .out(Output15));
  Multiplexer #(.select(4), .width(32), .enable("false")) multiplexer_1 (
    .in0(Output0), .in1(Output1), .in2(Output2), .in3(Output3), .in4(Output4), .in5(Output5), .in6(Output6),
    .in7(Output7), .in8(Output8), .in9(Output9), .in10(Output10), .in11(Output11), .in12(Output12),
    .in13({{31{1'b0}}, Output13[0]}), .in14(Output14), .in15({{25{1'b0}}, Output15}), .out(Result),
    .sel(ALUSel));

  // Notes on the sheet:
  //   INPUTS to your circuit
  //   DON'T CHANGE THE LOCATIONS OF THE INPUTS AND OUTPUTS!
  //   OUTPUT from your circuit
endmodule

module signed_multiplication (
  input  [31:0] in_1,
  input  [31:0] in_2,
  output [31:0] out_3,
  output [31:0] out_4
);

  wire xor_1_out;
  wire [31:0] multiplexer_1_out, multiplexer_2_out, multiplier_1_cout, multiplier_1_out, negator_1_out,
       negator_2_out, negator_3_out, negator_4_out, subtractor_1_out;

  Negator #(.width(32)) negator_1 (.in(in_1), .out(negator_1_out));
  Negator #(.width(32)) negator_2 (.in(in_2), .out(negator_2_out));
  Multiplexer #(.width(32), .enable("false")) multiplexer_1 (
    .in0(in_1), .in1(negator_1_out), .out(multiplexer_1_out), .sel(in_1[31]));
  Multiplexer #(.width(32), .enable("false")) multiplexer_2 (
    .in0(in_2), .in1(negator_2_out), .out(multiplexer_2_out), .sel(in_2[31]));
  Multiplier #(.width(32)) multiplier_1 (
    .a(multiplexer_1_out), .b(multiplexer_2_out), .out(multiplier_1_out), .cout(multiplier_1_cout));  // open: cin
  Negator #(.width(32)) negator_3 (.in(multiplier_1_cout), .out(negator_3_out));
  xor xor_1 (xor_1_out, in_2[31], in_1[31]);
  Subtractor #(.width(32)) subtractor_1 (.a(negator_3_out), .b(32'h1), .out(subtractor_1_out));  // open: bin, bout
  Negator #(.width(32)) negator_4 (.in(multiplier_1_out), .out(negator_4_out));
  Multiplexer #(.width(32), .enable("false")) multiplexer_3 (
    .in0(multiplier_1_cout), .in1(subtractor_1_out), .out(out_4), .sel(xor_1_out));
  Multiplexer #(.width(32), .enable("false")) multiplexer_4 (
    .in0(multiplier_1_out), .in1(negator_4_out), .out(out_3), .sel(xor_1_out));
endmodule

module signed_divide (
  input  [31:0] in_1,
  input  [31:0] in_2,
  output [31:0] out_3
);

  wire xor_1_out;
  wire [31:0] divider_1_out, multiplexer_1_out, multiplexer_2_out, negator_1_out, negator_2_out,
       negator_3_out;

  Negator #(.width(32)) negator_1 (.in(in_1), .out(negator_1_out));
  Negator #(.width(32)) negator_2 (.in(in_2), .out(negator_2_out));
  Multiplexer #(.width(32), .enable("false")) multiplexer_1 (
    .in0(in_1), .in1(negator_1_out), .out(multiplexer_1_out), .sel(in_1[31]));
  Multiplexer #(.width(32), .enable("false")) multiplexer_2 (
    .in0(in_2), .in1(negator_2_out), .out(multiplexer_2_out), .sel(in_2[31]));
  xor xor_1 (xor_1_out, in_2[31], in_1[31]);
  Divider #(.width(32)) divider_1 (
    .a(multiplexer_1_out), .b(multiplexer_2_out), .out(divider_1_out));  // open: upper, rem
  Negator #(.width(32)) negator_3 (.in(divider_1_out), .out(negator_3_out));
  Multiplexer #(.width(32), .enable("false")) multiplexer_3 (
    .in0(divider_1_out), .in1(negator_3_out), .out(out_3), .sel(xor_1_out));
endmodule

module signed_mul1 (
  input  [31:0] in1,
  input  [31:0] in2,
  output [31:0] o1,
  output [31:0] o2
);

  wire xor_1_out;
  wire [31:0] negator_1_out, negator_2_out, negator_3_out, subtractor_1_out;

  Negator #(.width(32)) negator_1 (.in(in2), .out(negator_1_out));
  Multiplier #(.width(32)) multiplier_1 (.a(in1), .b(in2), .out(o1), .cout(o2));  // open: cin
  Negator #(.width(32)) negator_2 (.in(o2), .out(negator_2_out));
  xor xor_1 (xor_1_out, in2[31], in1[31]);
  Subtractor #(.width(32)) subtractor_1 (.a(negator_2_out), .b(32'h1), .out(subtractor_1_out));  // open: bin, bout
  Negator #(.width(32)) negator_3 (.in(o1), .out(negator_3_out));
endmodule
