// Logisim project alu-mult.circ as structural Verilog: 1 circuit, main circuit main
module main (
  output [7:0] Test,
  output [31:0] Result,
  output [3:0] ALU_Sel,
  output [31:0] Input_A,
  output [31:0] Input_B
);

  wire clock_1_out;
  wire [7:0] adder_1_out;

  Clock clock_1 (.out(clock_1_out));
  Adder adder_1 (.a(8'h1), .b(Test), .out(adder_1_out));  // open: cin, cout
  Register register_1 (.D(adder_1_out), .clk(clock_1_out), .Q(Test));  // open: en, clr
  ROM #(.dataWidth(32)) rom_1 (.addr(Test), .data(Input_A));
  ROM #(.dataWidth(32)) rom_2 (.addr(Test), .data(Input_B));
  alu alu_1 (.A(Input_A), .B(Input_B), .ALUSel(ALU_Sel), .Result(Result));  // open: in_4, in_5, out_7
  ROM #(.dataWidth(4)) rom_3 (.addr(Test), .data(ALU_Sel));

  // Notes on the sheet:
  //   contents of rom_1 (hex, n*v repeats v):
  //   173 ffffdead ffffdead efffffff 3e41
  //   Your ALU must fit here!
  //   contents of rom_2 (hex, n*v repeats v):
  //   155 eefffffb ffffdead ac273deb fffface1
  //   There should be no red or blue wires, and the result should not be all X's
  //   contents of rom_3 (hex, n*v repeats v):
  //   5 5 5 6 6
endmodule
