// Logisim project cpu.circ as structural Verilog: 6 circuits, main circuit main
module main (
  input  [31:0] in_1,
  input  in_2,
  output [31:0] out_3,
  output [31:0] out_4,
  output [31:0] out_5,
  output [31:0] out_6,
  output [31:0] out_7,
  output [31:0] out_8,
  output [31:0] out_9,
  output [31:0] out_10,
  output [31:0] out_11
);

  wire and_1_out, BrEQ, BrEQ_signed, BrEQ_unsigned, BrLT, BrLT_signed, BrLT_unsigned, BrUn, comparator_1_eq,
       comparator_2_eq, comparator_3_eq, comparator_4_eq, jump_sel, MemRW, op_src, PC_sel, PC_src, Reg_we,
       sb_jump_1_if_jump;
  wire [1:0] d_src;
  wire [3:0] ALUSel;
  wire [4:0] multiplexer_3_out;
  wire [31:0] adder_1_out, adder_2_out, ALU_result, ex_inst, Imm, main_2_readdata, multiplexer_1_out,
       multiplexer_2_out, multiplexer_4_out, multiplexer_5_out, PC, Read_Data_1, Read_Data_2, ReadData,
       register_3_q, register_4_q, shifter_2_out, undriven, Write_Data;

  Adder #(.width(32)) adder_1 (.a(PC), .b(32'h4), .out(adder_1_out));  // open: cin, cout
  Register #(.width(32)) register_1 (.D(multiplexer_1_out), .clk(in_2), .Q(ex_inst));  // open: en, clr
  Multiplexer #(.width(32), .enable("false")) multiplexer_1 (
    .in0(in_1), .in1(32'h13), .out(multiplexer_1_out), .sel(jump_sel));
  Multiplexer #(.width(32), .enable("false")) multiplexer_2 (
    .in0(adder_1_out), .in1(ALU_result), .out(multiplexer_2_out), .sel(jump_sel));
  Register #(.width(32)) register_2 (.D(multiplexer_2_out), .clk(in_2), .Q(PC));  // open: en, clr
  Shifter #(.width(32), .shift("lr")) shifter_1 (.in(PC), .\dist (5'b00010), .out(out_3));
  Comparator #(.width(7), .mode("unsigned")) comparator_1 (
    .a(ex_inst[6:0]), .b(7'b0110111), .eq(comparator_1_eq));  // open: gt, lt
  Comparator #(.width(5)) comparator_2 (.a(ex_inst[6:2]), .b(5'b11000), .eq(comparator_2_eq));  // open: gt, lt
  Comparator #(.width(5)) comparator_3 (.a(ex_inst[6:2]), .b(5'b11011), .eq(comparator_3_eq));  // open: gt, lt
  Comparator #(.width(5)) comparator_4 (.a(ex_inst[6:2]), .b(5'b11001), .eq(comparator_4_eq));  // open: gt, lt
  and and_1 (and_1_out, comparator_2_eq, sb_jump_1_if_jump);
  SB_Jump sb_jump_1 (.BrLt(BrLT), .BrEq(BrEQ), .Func3(ex_inst[14:12]), .If_Jump(sb_jump_1_if_jump));
  or or_1 (jump_sel, comparator_3_eq, comparator_4_eq, and_1_out);
  Multiplexer #(.width(5), .enable("false")) multiplexer_3 (
    .in0(ex_inst[19:15]), .in1({5{1'b0}}), .out(multiplexer_3_out), .sel(comparator_1_eq));
  ImmGen immgen_1 (.Output_Imm(Imm), .Instruction(ex_inst));
  regfile_main main_1 (
    .rs2(ex_inst[24:20]), .rd(ex_inst[11:7]), .Read_Data_1(Read_Data_1), .Read_Data_2(Read_Data_2),
    .ra(out_4), .sp(out_5), .t0(out_6), .t1(out_7), .t2(out_8), .s0(out_9), .s1(out_10), .a0(out_11),
    .rs1(multiplexer_3_out), .Write_Data(Write_Data), .RegWEn(Reg_we), .clk(in_2));
  Register #(.width(32)) register_3 (.D(PC), .clk(in_2), .Q(register_3_q));  // open: en, clr
  Comparator #(.width(32)) comparator_5 (
    .a(Read_Data_1), .b(Read_Data_2), .eq(BrEQ_signed), .lt(BrLT_signed));  // open: gt
  Comparator #(.width(32), .mode("unsigned")) comparator_6 (
    .a(Read_Data_1), .b(Read_Data_2), .eq(BrEQ_unsigned), .lt(BrLT_unsigned));  // open: gt
  Multiplexer #(.width(32), .enable("false")) multiplexer_4 (
    .in0(Read_Data_1), .in1(register_3_q), .out(multiplexer_4_out), .sel(PC_src));
  Multiplexer #(.width(32), .enable("false")) multiplexer_5 (
    .in0(Imm), .in1(Read_Data_2), .out(multiplexer_5_out), .sel(op_src));
  Control control_1 (
    .Inst({ex_inst[30], ex_inst[25], ex_inst[14:12], ex_inst[6:2]}), .BrLT(BrLT), .BrEQ(BrEQ),
    .pc_sel(PC_sel), .BrUN(BrUn), .alu_sel(ALUSel), .pc_src(PC_src), .op_src(op_src), .mem_rw(MemRW),
    .reg_we(Reg_we), .d_src(d_src));
  Shifter #(.width(32), .shift("ar")) shifter_2 (.in(undriven), .\dist (5'b00010), .out(shifter_2_out));
  Multiplexer #(.width(32), .enable("false")) multiplexer_6 (.in1(shifter_2_out), .sel(jump_sel));  // open: in0, out
  Multiplexer #(.enable("false")) multiplexer_7 (.in0(BrEQ_signed), .in1(BrEQ_unsigned), .out(BrEQ), .sel(BrUn));
  mem_main main_2 (
    .WriteAddr(ALU_result), .WriteData(Read_Data_2), .MemRW(MemRW), .ReadData(main_2_readdata), .clk(in_2));
  Multiplexer #(.enable("false")) multiplexer_8 (.in0(BrLT_signed), .in1(BrLT_unsigned), .out(BrLT), .sel(BrUn));
  alu alu_1 (.A(multiplexer_4_out), .B(multiplexer_5_out), .ALUSel(ALUSel), .Result(ALU_result));
  RamReadCtrl ramreadctrl_1 (.Data(main_2_readdata), .Funct3(ex_inst[14:12]), .OutputData(ReadData));
  Register #(.width(32)) register_4 (.D(PC), .clk(in_2), .Q(register_4_q));  // open: en, clr
  Multiplexer #(.select(2), .width(32), .enable("false")) multiplexer_9 (
    .in0(ReadData), .in1(ALU_result), .in2(adder_2_out), .out(Write_Data), .sel(d_src));  // open: in3
  Adder #(.width(32)) adder_2 (.a(register_4_q), .b(32'h4), .out(adder_2_out));  // open: cin, cout

  // Other names for the same wires on the sheet: a0[31:0] = out_11; clk = in_2; fetch_addr[31:0] = out_3;
  //   INSTRUCTION[31:0] = in_1; ra[31:0] = out_4; s0[31:0] = out_9; s1[31:0] = out_10; sp[31:0] = out_5;
  //   t0[31:0] = out_6; t1[31:0] = out_7; t2[31:0] = out_8

  // Notes on the sheet:
  //   Output
  //   pipeline
  //   Inputs/Outputs from run.circ. DO NOT MOVE THESE.
  //   Inputs
  //   It is OK to move the PC, RegFile, ALU, and MEM to wherever is most convenient for you when constructing your CPU, and to delete this text
  //   jump select
  //   Inputs/Outputs from run.circ. DO NOT MOVE THESE.
endmodule

module ImmGen (
  input  [31:0] Instruction,
  output [31:0] Output_Imm
);

  wire comparator_1_eq, comparator_2_eq, comparator_3_eq, comparator_4_eq, comparator_5_eq, comparator_6_eq,
       comparator_7_eq, comparator_8_eq, or_1_out, or_2_out;
  wire [31:0] adder_1_out, adder_2_out, adder_3_out, bit_extender_1_out, bit_extender_2_out,
       bit_extender_3_out, bit_extender_4_out, multiplexer_1_out, multiplexer_2_out, multiplexer_3_out,
       multiplexer_4_out, multiplexer_5_out;

  Comparator #(.width(7), .mode("unsigned")) comparator_1 (
    .a(Instruction[6:0]), .b(7'b0000011), .eq(comparator_1_eq));  // open: gt, lt
  Comparator #(.width(7), .mode("unsigned")) comparator_2 (
    .a(Instruction[6:0]), .b(7'b0010011), .eq(comparator_2_eq));  // open: gt, lt
  Comparator #(.width(7), .mode("unsigned")) comparator_3 (
    .a(Instruction[6:0]), .b(7'b1100111), .eq(comparator_3_eq));  // open: gt, lt
  assign bit_extender_1_out = {{20{Instruction[31]}}, {Instruction[31:25], Instruction[11:7]}};  // Bit_Extender bit_extender_1
  Comparator #(.width(7), .mode("unsigned")) comparator_4 (
    .a(Instruction[6:0]), .b(7'b0100011), .eq(comparator_4_eq));  // open: gt, lt
  Multiplexer #(.width(32), .enable("false")) multiplexer_1 (
    .in0({32{1'b0}}), .in1(bit_extender_1_out), .out(multiplexer_1_out), .sel(comparator_4_eq));
  assign bit_extender_2_out = {{19{Instruction[31]}}, {Instruction[31], Instruction[7], Instruction[30:25], Instruction[11:8], 1'b0}};  // Bit_Extender bit_extender_2
  Comparator #(.width(7), .mode("unsigned")) comparator_5 (
    .a(Instruction[6:0]), .b(7'b1100011), .eq(comparator_5_eq));  // open: gt, lt
  Comparator #(.width(7), .mode("unsigned")) comparator_6 (
    .a(Instruction[6:0]), .b(7'b0010111), .eq(comparator_6_eq));  // open: gt, lt
  Comparator #(.width(7), .mode("unsigned")) comparator_7 (
    .a(Instruction[6:0]), .b(7'b0110111), .eq(comparator_7_eq));  // open: gt, lt
  Comparator #(.width(7), .mode("unsigned")) comparator_8 (
    .a(Instruction[6:0]), .b(7'b1101111), .eq(comparator_8_eq));  // open: gt, lt
  or or_1 (or_1_out, comparator_1_eq, comparator_2_eq, comparator_3_eq);
  or or_2 (or_2_out, comparator_6_eq, comparator_7_eq);
  assign bit_extender_3_out = {{11{Instruction[31]}}, {Instruction[31], Instruction[19:12], Instruction[20], Instruction[30:21], 1'b0}};  // Bit_Extender bit_extender_3
  Multiplexer #(.width(32), .enable("false")) multiplexer_2 (
    .in0({32{1'b0}}), .in1(bit_extender_3_out), .out(multiplexer_2_out), .sel(comparator_8_eq));
  assign bit_extender_4_out = {{20{Instruction[31]}}, Instruction[31:20]};  // Bit_Extender bit_extender_4
  Multiplexer #(.width(32), .enable("false")) multiplexer_3 (
    .in0({32{1'b0}}), .in1(bit_extender_4_out), .out(multiplexer_3_out), .sel(or_1_out));
  Multiplexer #(.width(32), .enable("false")) multiplexer_4 (
    .in0({32{1'b0}}), .in1(bit_extender_2_out), .out(multiplexer_4_out), .sel(comparator_5_eq));
  Multiplexer #(.width(32), .enable("false")) multiplexer_5 (
    .in0({32{1'b0}}), .in1({Instruction[31:12], {12{1'b0}}}), .out(multiplexer_5_out), .sel(or_2_out));
  Adder #(.width(32)) adder_1 (.a(multiplexer_3_out), .b(multiplexer_1_out), .out(adder_1_out));  // open: cin, cout
  Adder #(.width(32)) adder_2 (.a(multiplexer_4_out), .b(multiplexer_5_out), .out(adder_2_out));  // open: cin, cout
  Adder #(.width(32)) adder_3 (.a(adder_2_out), .b(multiplexer_2_out), .out(adder_3_out));  // open: cin, cout
  Adder #(.width(32)) adder_4 (.a(adder_1_out), .b(adder_3_out), .out(Output_Imm));  // open: cin, cout

  // Other names for the same wires on the sheet: Opcode[6:0] = Instruction[6:0]

  // Notes on the sheet:
  //   S type
  //   I type
  //   U type
  //   SB type
  //   UJ type
endmodule

module m1 (
  input  [31:0] in_1,
  input  in_2,
  output [31:0] out_3,
  output [31:0] out_4,
  output [31:0] out_5,
  output [31:0] out_6,
  output [31:0] out_7,
  output [31:0] out_8,
  output [31:0] out_9,
  output [31:0] out_10,
  output [31:0] out_11
);

  wire and_1_out, BeEQ, BeLT, BrEQ, BrEQ_signed, BrEQ_unsigned, BrLT, BrLT_signed, BrLT_unsigned, BrUn,
       comparator_1_eq, comparator_2_eq, comparator_3_eq, jump_sel, MemRW, op_src, PC_sel, PC_src, Reg_we;
  wire [1:0] d_src;
  wire [3:0] ALUSel;
  wire [4:0] rd, rs1, rs2;
  wire [30:2] Instruction_t;
  wire [31:0] ALU_result, ex_inst, Imm, multiplexer_1_out, multiplexer_2_out, multiplexer_3_out,
       multiplexer_4_out, PC_plus4, Read_Data_1, Read_Data_2, ReadData, Write_Data;

  Adder #(.width(32)) adder_1 (.a(out_3), .b(32'h1), .out(PC_plus4));  // open: cin, cout
  Register #(.width(32)) register_1 (.D(multiplexer_1_out), .clk(in_2), .Q(ex_inst));  // open: en, clr
  Multiplexer #(.width(32), .enable("false")) multiplexer_1 (
    .in0(in_1), .in1(32'h13), .out(multiplexer_1_out), .sel(jump_sel));
  Multiplexer #(.width(32), .enable("false")) multiplexer_2 (
    .in0(PC_plus4), .in1(ALU_result), .out(multiplexer_2_out), .sel(PC_sel));
  Register #(.width(32)) register_2 (.D(multiplexer_2_out), .clk(in_2), .Q(out_3));  // open: en, clr
  Comparator #(.width(5)) comparator_1 (.a(in_1[6:2]), .b(5'b11000), .eq(comparator_1_eq));  // open: gt, lt
  Comparator #(.width(5)) comparator_2 (.a(in_1[6:2]), .b(5'b11011), .eq(comparator_2_eq));  // open: gt, lt
  Comparator #(.width(5)) comparator_3 (.a(in_1[6:2]), .b(5'b11001), .eq(comparator_3_eq));  // open: gt, lt
  buf and_1 (and_1_out, comparator_1_eq);  // AND_Gate
  or or_1 (jump_sel, comparator_2_eq, comparator_3_eq, and_1_out);
  ImmGen immgen_1 (.Output_Imm(Imm), .Instruction(ex_inst));
  regfile_main main_1 (
    .rs2(rs2), .rd(rd), .Read_Data_1(Read_Data_1), .Read_Data_2(Read_Data_2), .ra(out_4), .sp(out_5),
    .t0(out_6), .t1(out_7), .t2(out_8), .s0(out_9), .s1(out_10), .a0(out_11), .rs1(rs1),
    .Write_Data(Write_Data), .RegWEn(Reg_we), .clk(in_2));
  Comparator #(.width(32)) comparator_4 (
    .a(Read_Data_1), .b(Read_Data_2), .eq(BrEQ_signed), .lt(BrLT_signed));  // open: gt
  Comparator #(.width(32), .mode("unsigned")) comparator_5 (
    .a(Read_Data_1), .b(Read_Data_2), .eq(BrEQ_unsigned), .lt(BrLT_unsigned));  // open: gt
  Multiplexer #(.width(32), .enable("false")) multiplexer_3 (
    .in0(Read_Data_1), .in1(out_3), .out(multiplexer_3_out), .sel(PC_src));
  Multiplexer #(.width(32), .enable("false")) multiplexer_4 (
    .in0(Imm), .in1(Read_Data_2), .out(multiplexer_4_out), .sel(op_src));
  // Control control_1: pin names not known; wires that end beside it: {Instruction_t[30], Instruction_t[25], Instruction_t[14:12], Instruction_t[6:2]}, BeLT, BeEQ, PC_sel, BrUn, PC_src, op_src, ALUSel, MemRW, Reg_we, d_src
  Multiplexer #(.enable("false")) multiplexer_5 (.in0(BrEQ_signed), .in1(BrEQ_unsigned), .out(BrEQ), .sel(BrUn));
  mem_main main_2 (.WriteAddr(ALU_result), .WriteData(Read_Data_2), .MemRW(MemRW), .ReadData(ReadData), .clk(in_2));
  alu alu_1 (.A(multiplexer_3_out), .B(multiplexer_4_out), .ALUSel(ALUSel), .Result(ALU_result));
  Multiplexer #(.enable("false")) multiplexer_6 (.in0(BrLT_signed), .in1(BrLT_unsigned), .out(BrLT), .sel(BrUn));
  Multiplexer #(.select(2), .width(32), .enable("false")) multiplexer_7 (
    .in0(ReadData), .in1(ALU_result), .in2(PC_plus4), .out(Write_Data), .sel(d_src));  // open: in3

  // Other names for the same wires on the sheet: a0[31:0] = out_11; clk = in_2; fetch_addr[31:0] = out_3;
  //   PC[31:0] = out_3; INSTRUCTION[31:0] = in_1; ra[31:0] = out_4; s0[31:0] = out_9; s1[31:0] = out_10;
  //   sp[31:0] = out_5; t0[31:0] = out_6; t1[31:0] = out_7; t2[31:0] = out_8

  // Notes on the sheet:
  //   Output
  //   pipeline
  //   Inputs/Outputs from run.circ. DO NOT MOVE THESE.
  //   Inputs
  //   It is OK to move the PC, RegFile, ALU, and MEM to wherever is most convenient for you when constructing your CPU, and to delete this text
  //   jump select
  //   Inputs/Outputs from run.circ. DO NOT MOVE THESE.
endmodule

module Control (
  input  [9:0] Inst,
  input  BrLT,
  input  BrEQ,
  output pc_sel,
  output BrUN,
  output [3:0] alu_sel,
  output pc_src,
  output op_src,
  output mem_rw,
  output reg_we,
  output [1:0] d_src
);

  wire comparator_1_eq, comparator_2_eq, comparator_3_eq, comparator_4_eq, comparator_5_eq, comparator_6_eq,
       comparator_7_eq, comparator_8_eq, comparator_9_eq, comparator_10_eq, comparator_11_eq,
       comparator_12_eq, comparator_13_eq, comparator_14_eq, comparator_15_eq, comparator_16_eq,
       comparator_17_eq, or_1_out;

  Comparator #(.width(5)) comparator_1 (.a(Inst[4:0]), .b(5'b11011), .eq(comparator_1_eq));  // open: gt, lt
  Comparator #(.width(5)) comparator_2 (.a(Inst[4:0]), .b(5'b11001), .eq(comparator_2_eq));  // open: gt, lt
  Comparator #(.width(5)) comparator_3 (.a(Inst[4:0]), .b(5'b00101), .eq(comparator_3_eq));  // open: gt, lt
  Comparator #(.width(5)) comparator_4 (.a(Inst[4:0]), .b(5'b01101), .eq(comparator_4_eq));  // open: gt, lt
  Comparator #(.width(5)) comparator_5 (.a(Inst[4:0]), .b(5'b11000), .eq(comparator_5_eq));  // open: gt, lt
  Comparator #(.width(5)) comparator_6 (.a(Inst[4:0]), .b(5'b11011), .eq(comparator_6_eq));  // open: gt, lt
  Comparator #(.width(5)) comparator_7 (.a(Inst[4:0]), .b(5'b11001), .eq(comparator_7_eq));  // open: gt, lt
  Comparator #(.width(5)) comparator_8 (.a(Inst[4:0]), .b(5'b11000), .eq(comparator_8_eq));  // open: gt, lt
  Comparator #(.width(5)) comparator_9 (.a(Inst[4:0]), .b(5'b00101), .eq(comparator_9_eq));  // open: gt, lt
  Comparator #(.width(5)) comparator_10 (.a(Inst[4:0]), .b(5'b11011), .eq(comparator_10_eq));  // open: gt, lt
  Comparator #(.width(5)) comparator_11 (.a(Inst[4:0]), .b(5'b11001), .eq(comparator_11_eq));  // open: gt, lt
  Comparator #(.width(5)) comparator_12 (.a(Inst[4:0]), .b(5'b01100), .eq(comparator_12_eq));  // open: gt, lt
  Comparator #(.width(5)) comparator_13 (.a(Inst[4:0]), .b({5{1'b0}}), .eq(comparator_13_eq));  // open: gt, lt
  Comparator #(.width(5)) comparator_14 (.a(Inst[4:0]), .b(5'b00100), .eq(comparator_14_eq));  // open: gt, lt
  Comparator #(.width(5)) comparator_15 (.a(Inst[4:0]), .b({5{1'b0}}), .eq(comparator_15_eq));  // open: gt, lt
  Comparator #(.width(5)) comparator_16 (.a(Inst[4:0]), .b(5'b11011), .eq(comparator_16_eq));  // open: gt, lt
  Comparator #(.width(5)) comparator_17 (.a(Inst[4:0]), .b(5'b11001), .eq(comparator_17_eq));  // open: gt, lt
  Comparator #(.width(5)) comparator_18 (.a(Inst[4:0]), .b(5'b01100), .eq(op_src));  // open: gt, lt
  Comparator #(.width(5)) comparator_19 (.a(Inst[4:0]), .b(5'b01000), .eq(mem_rw));  // open: gt, lt
  or or_1 (or_1_out, comparator_15_eq, d_src[1]);
  or or_2 (pc_sel, comparator_5_eq, comparator_6_eq, comparator_7_eq);
  or or_3 (pc_src, comparator_8_eq, comparator_9_eq, comparator_10_eq);
  or or_4 (reg_we, comparator_12_eq, comparator_13_eq, comparator_14_eq, comparator_3_eq, comparator_4_eq, comparator_1_eq, comparator_2_eq);
  not not_1 (d_src[0], or_1_out);
  or or_5 (d_src[1], comparator_16_eq, comparator_17_eq);
  ROM #(.addrWidth(10), .dataWidth(4)) rom_1 (.addr({Inst[4:0], Inst[9:5]}), .data(alu_sel));

  assign BrUN = Inst[6];

  // Other names for the same wires on the sheet: BeEQ = BrEQ

  // Notes on the sheet:
  //   contents of rom_1 (hex, n*v repeats v):
  //   3 3 3 0 3 3 0 0 3 3 3 0 3 3 0 0 3 3 3 0 3 3 0 0 3 3 3 0 3 3 98*0 3 e d 0 2 b 1 0 3 0 d 0 2 0 1 0 3 0
  //   d 0 2 0 1 0 3 0 d 0 2 0 1 0 32*3 66*0 3 7*0 3 7*0 3 7*0 3 101*0 3 e 0 0 2 b 1 0 5 7 0 6 9 8 0 a 4
  //   15*0 32*3 320*0 3 3 0 0 3 0 4*3 0 0 3 0 4*3 0 0 3 0 4*3 0 0 3 0 3 3 3 7*0 3 7*0 3 7*0 3 39*0 32*3
endmodule

module SB_Jump (
  input  BrLt,
  input  BrEq,
  input  [2:0] Func3,
  output If_Jump
);

  wire beq_out, bgeu_out, blt_out, bltu_out, bne_out, not_1_out, not_2_out, not_3_out, not_4_out, not_5_out,
       not_6_out, not_7_out, not_8_out, not_9_out, not_10_out;

  not not_1 (not_1_out, Func3[2]);
  not not_2 (not_2_out, Func3[1]);
  not not_3 (not_3_out, Func3[0]);
  not not_4 (not_4_out, BrEq);
  not not_5 (not_5_out, BrLt);
  not not_6 (not_6_out, Func3[2]);
  not not_7 (not_7_out, Func3[1]);
  not not_8 (not_8_out, BrEq);
  not not_9 (not_9_out, BrLt);
  and beq (beq_out, not_1_out, not_2_out, not_3_out, BrEq);
  not not_10 (not_10_out, Func3[0]);
  and bne (bne_out, not_6_out, not_7_out, Func3[0], not_8_out);
  and bgeu (bgeu_out, Func3[2], Func3[1], Func3[0], not_9_out);
  and blt (blt_out, Func3[2], not_2_out, not_10_out, BrLt, not_4_out);
  and bltu (bltu_out, Func3[2], Func3[1], BrLt, not_3_out, not_4_out);
  or or_1 (If_Jump, beq_out, blt_out, bltu_out, bne_out, bgeu_out);
endmodule

module RamReadCtrl (
  input  [31:0] Data,
  input  [2:0] Funct3,
  output [31:0] OutputData
);

  wire [31:0] bit_extender_1_out, bit_extender_2_out, bit_extender_3_out, bit_extender_4_out;

  assign bit_extender_1_out = {{24{Data[7]}}, Data[7:0]};  // Bit_Extender bit_extender_1
  assign bit_extender_2_out = {{16{Data[15]}}, Data[15:0]};  // Bit_Extender bit_extender_2
  assign bit_extender_3_out = {{24{1'b0}}, Data[7:0]};  // Bit_Extender bit_extender_3
  assign bit_extender_4_out = {{16{1'b0}}, Data[15:0]};  // Bit_Extender bit_extender_4
  Multiplexer #(.select(3), .width(32), .enable("false")) multiplexer_1 (
    .in0(bit_extender_1_out), .in1(bit_extender_2_out), .in2(Data), .in4(bit_extender_3_out),
    .in5(bit_extender_4_out), .out(OutputData), .sel(Funct3));  // open: in3, in6, in7
endmodule
