// Logisim project alu-comprehensive.circ as structural Verilog: 1 circuit, main circuit main
module main (
  output [7:0] Test,
  output [31:0] Result,
  output [3:0] ALU_Sel,
  output [31:0] Input_A,
  output [31:0] Input_B
);

  wire clock_1_out;
  wire [7:0] adder_1_out;

  Clock clock_1 (.out(clock_1_out));
  Adder adder_1 (.a(8'h1), .b(Test), .out(adder_1_out));  // open: cin, cout
  Register register_1 (.D(adder_1_out), .clk(clock_1_out), .Q(Test));  // open: en, clr
  ROM #(.dataWidth(32)) rom_1 (.addr(Test), .data(Input_A));
  ROM #(.dataWidth(32)) rom_2 (.addr(Test), .data(Input_B));
  alu alu_1 (.A(Input_A), .B(Input_B), .ALUSel(ALU_Sel), .Result(Result));  // open: in_4, in_5, out_7
  ROM #(.dataWidth(4)) rom_3 (.addr(Test), .data(ALU_Sel));

  // Notes on the sheet:
  //   contents of rom_1 (hex, n*v repeats v):
  //   ffff0000 10101010 ffff0000 10101010 ffff0000 10101010 ffffffff 5 4 ffff0007 ffffabcd ffffffff
  //   ffffabcd ffffffff ffffabcd ffffffff ffffbeef 6 1ab1462 f8adbcd3 1 f8adbcd3 4*f234567f ffffabcd 5
  //   ffff0fff 1f123321 fff10101 f4924080
  //   Your ALU must fit here!
  //   contents of rom_2 (hex, n*v repeats v):
  //   dcba0000 1010 dcba0000 1010 dcba0000 1010 ffffbeef aa 3 ffff0009 ffffffff ffffabcd ffffffff ffffabcd
  //   ffffffff ffffabcd 6 ffffbeef 5102 2 5 2 9 fe9 9 fe9 5 ffffabcd fff0ffff 2fa58965 f0fff021 102492f
  //   There should be no red or blue wires, and the result should not be all X's
  //   contents of rom_3 (hex, n*v repeats v):
  //   0 0 1 1 2 2 3 3 4 4 5 5 6 6 7 7 8 8 9 9 a a b b c c d d e e f f
endmodule
